// Logisim project Detector_de_Numero_Primo_Crie_um_circuito_que_detecte_se_uma_entrada_binária_de_4.circ as structural Verilog: 1 circuit, main circuit Detector de Número Primo: Crie um circuito que detecte se uma entrada binária de 4 bits representa um número primo. Utilize portas lógicas e mapas de Karnaugh para simplificar o circuito.
module \Detector_de_Número_Primo__Crie_um_circuito_que_detecte_se_uma_entrada_binária_de_4_bits_representa_um_número_primo__Utilize_portas_lógicas_e_mapas_de_Karnaugh_para_simplificar_o_circuito  (
  input  A,
  input  B,
  input  C,
  input  D,
  output Saida
);

  wire and_2_out, AND_out, not_1_out, not_2_out, not_3_out, OR_out, XOR_out;

  not not_1 (not_1_out, B);
  not not_2 (not_2_out, A);
  not not_3 (not_3_out, D);
  or OR (OR_out, not_1_out, D);
  xor XOR (XOR_out, B, C);
  and AND (AND_out, OR_out, not_2_out, C);
  and and_2 (and_2_out, D, XOR_out);
  or OR_2 (Saida, AND_out, and_2_out);
endmodule
