// Logisim project Trabalho_AOC_Leonam_e_kauã..circ as structural Verilog: 23 circuits, main circuit Somador de bit
module Multiplexador (
  input  W0,
  input  W1,
  input  W2,
  input  W3,
  input  S0,
  input  S1,
  output Saida
);

  wire AND_2_out, AND_3_out, AND_4_out, AND_out, NOT_2_out, NOT_out;

  not NOT (NOT_out, S0);
  not NOT_2 (NOT_2_out, S1);
  and AND (AND_out, W0, NOT_out, NOT_2_out);
  and AND_2 (AND_2_out, W1, S0, NOT_2_out);
  and AND_3 (AND_3_out, W2, NOT_out, S1);
  and AND_4 (AND_4_out, W3, S0, S1);
  or OR (Saida, AND_out, AND_2_out, AND_3_out, AND_4_out);
endmodule

// XOR
module \Porta_lógica_XOR_usando_os_componentes__AND__NOT__e_OR  (
  input  A,
  input  B,
  output SAIDA
);

  wire AND_2_out, AND_out, not_1_out, not_2_out;

  not not_1 (not_1_out, A);
  not not_2 (not_2_out, B);
  and AND (AND_out, not_1_out, B);
  and AND_2 (AND_2_out, A, not_2_out);
  or OR (SAIDA, AND_out, AND_2_out);
endmodule

// +1Bit
module Somador_de_bit (
  input  C_in,
  input  A,
  input  B,
  output Saida,
  output C_out
);

  wire and_2_out, and_3_out, AND_out, NOR_out;

  xor NOR (NOR_out, A, B);
  and AND (AND_out, C_in, A);
  and and_2 (and_2_out, C_in, B);
  and and_3 (and_3_out, B, A);
  xor xor_1 (Saida, NOR_out, C_in);
  or OR (C_out, AND_out, and_2_out, and_3_out);
endmodule

module Somador_de_8_bits (
  input  [7:0] A,
  input  C_in,
  input  [7:0] B,
  output C_OUT_1,
  output C_OUT_2,
  output C_OUT_3,
  output C_OUT_4,
  output [7:0] SAIDA,
  output C_OUT_5,
  output C_OUT_6,
  output C_OUT_7,
  output C_OUT_8
);

  Somador_de_bit somador_de_bit_1 (.A(A[0]), .B(B[0]), .C_in(C_in), .C_out(C_OUT_1), .Saida(SAIDA[0]));
  Somador_de_bit somador_de_bit_2 (.A(A[1]), .B(B[1]), .C_in(C_OUT_1), .C_out(C_OUT_2), .Saida(SAIDA[1]));
  Somador_de_bit somador_de_bit_3 (.A(A[2]), .B(B[2]), .C_in(C_OUT_2), .C_out(C_OUT_3), .Saida(SAIDA[2]));
  Somador_de_bit somador_de_bit_4 (.A(A[3]), .B(B[3]), .C_in(C_OUT_3), .C_out(C_OUT_4), .Saida(SAIDA[3]));
  Somador_de_bit somador_de_bit_5 (.A(A[4]), .B(B[4]), .C_in(C_OUT_4), .C_out(C_OUT_5), .Saida(SAIDA[4]));
  Somador_de_bit somador_de_bit_6 (.A(A[5]), .B(B[5]), .C_in(C_OUT_5), .C_out(C_OUT_6), .Saida(SAIDA[5]));
  Somador_de_bit somador_de_bit_7 (.A(A[6]), .B(B[6]), .C_in(C_OUT_6), .C_out(C_OUT_7), .Saida(SAIDA[6]));
  Somador_de_bit somador_de_bit_8 (.A(A[7]), .B(B[7]), .C_in(C_OUT_7), .C_out(C_OUT_8), .Saida(SAIDA[7]));

  // Notes on the sheet:
  //   01111111 + 00000001 = 10000000
  //   127   + 1 = 128
  //   011111111 + 00000001 = 00000000
  //   255 + 1  = Overflow
endmodule

module \Memória_ROM_de_8_bits  (
  input  A0,
  input  A1,
  input  A2,
  output [7:0] SAIDA
);

  wire AND_2_out, AND_3_out, AND_4_out, AND_5_out, AND_6_out, AND_7_out, AND_8_out, AND_out, not_1_out,
       not_2_out, not_3_out, not_4_out, not_5_out, not_6_out, not_7_out, not_8_out, not_9_out, not_10_out,
       not_11_out, not_12_out;

  not not_1 (not_1_out, A0);
  not not_2 (not_2_out, A1);
  not not_3 (not_3_out, A1);
  not not_4 (not_4_out, A0);
  not not_5 (not_5_out, A2);
  and AND (AND_out, not_4_out, not_3_out, A2);
  and AND_2 (AND_2_out, not_1_out, not_2_out, not_5_out);
  not not_6 (not_6_out, A0);
  and AND_3 (AND_3_out, not_6_out, A1, not_7_out);
  not not_7 (not_7_out, A2);
  not not_8 (not_8_out, A0);
  and AND_4 (AND_4_out, not_8_out, A1, A2);
  not not_9 (not_9_out, A2);
  not not_10 (not_10_out, A1);
  and AND_5 (AND_5_out, A0, not_10_out, not_9_out);
  not not_11 (not_11_out, A1);
  and AND_6 (AND_6_out, A0, not_11_out, A2);
  not not_12 (not_12_out, A2);
  and AND_7 (AND_7_out, A0, A1, not_12_out);
  and AND_8 (AND_8_out, A2, A1, A0);
  or OR (SAIDA[0], AND_2_out, AND_3_out, AND_6_out);
  buf OR_2 (SAIDA[1], AND_out);  // OR_Gate
  or OR_3 (SAIDA[2], AND_7_out, AND_4_out, AND_8_out);
  or OR_4 (SAIDA[3], AND_5_out, AND_4_out);
  or OR_5 (SAIDA[4], AND_2_out, AND_8_out);
  or OR_6 (SAIDA[5], AND_7_out, AND_out);
  or OR_7 (SAIDA[6], AND_out, AND_6_out);
  or OR_8 (SAIDA[7], AND_8_out, AND_2_out);
endmodule

module \Contador_Síncrono  (
  output [3:0] out_1
);

  wire clock_1_out, flip_flop_d_1_nq, flip_flop_d_2_p2, flip_flop_d_3_p2, flip_flop_d_4_p2, nand_1_out,
       nand_2_out;

  Clock clock_1 (.out(clock_1_out));
  Flip_flop_D flip_flop_d_1 (.D(clock_1_out), .Q(out_1[0]), .nQ(flip_flop_d_1_nq));
  // Flip_flop_D flip_flop_d_2: pin names not known; wires that end beside it: clock_1_out, flip_flop_d_2_p2, out_1[1]
  // Flip_flop_D flip_flop_d_3: pin names not known; wires that end beside it: clock_1_out, flip_flop_d_3_p2, out_1[2]
  // Flip_flop_D flip_flop_d_4: pin names not known; wires that end beside it: clock_1_out, flip_flop_d_4_p2, out_1[3]
  xor xor_1 (flip_flop_d_2_p2, out_1[0], out_1[1]);
  xor xor_2 (flip_flop_d_3_p2, nand_1_out, out_1[3]);
  nand nand_1 (nand_1_out, out_1[0], out_1[1]);
  xor xor_3 (flip_flop_d_4_p2, out_1[3], nand_2_out);
  nand nand_2 (nand_2_out, out_1[1], out_1[0], out_1[3]);
endmodule

module JK (
  input  J,
  input  K,
  output Q,
  output nQ
);

  wire button_1_out, CLK_out, nand_1_out, nand_2_out, nand_3_out, nand_4_out, nand_5_out, nand_6_out,
       not_1_out, not_2_out;

  Clock CLK (.out(CLK_out));
  nand nand_1 (nand_1_out, J, nQ, CLK_out);
  nand nand_2 (nand_2_out, CLK_out, Q, K);
  not not_1 (not_1_out, CLK_out);
  nand nand_3 (nand_3_out, nand_1_out, nand_4_out);
  nand nand_4 (nand_4_out, nand_3_out, not_2_out, nand_2_out);
  not not_2 (not_2_out, button_1_out);
  Button button_1 (.out(button_1_out));
  nand nand_5 (nand_5_out, nand_3_out, not_1_out);
  nand nand_6 (nand_6_out, not_1_out, nand_4_out);
  nand nand_7 (Q, nand_5_out, nQ);
  nand nand_8 (nQ, Q, not_2_out, nand_6_out);
endmodule

module Flip_flop_D (
  input  D,
  output Q,
  output nQ
);

  wire CLK_out, nand_1_out, nand_2_out, nand_3_out, nand_4_out, nand_5_out, nand_6_out, not_1_out;

  Clock CLK (.out(CLK_out));
  nand nand_1 (nand_1_out, D, CLK_out);
  nand nand_2 (nand_2_out, CLK_out, nand_1_out);
  not not_1 (not_1_out, CLK_out);
  nand nand_3 (nand_3_out, nand_1_out, nand_4_out);
  nand nand_4 (nand_4_out, nand_3_out, nand_2_out);
  nand nand_5 (nand_5_out, nand_3_out, not_1_out);
  nand nand_6 (nand_6_out, not_1_out, nand_5_out);
  nand nand_7 (Q, nand_5_out, nQ);
  nand nand_8 (nQ, Q, nand_6_out);
endmodule

module \Decodificador_de_7_Segmentos__Projete_um_circuito_que_converta_um_número_binário_de_4_bits_para_os_sinais_necessários_para_acionar_um_display_de_7_segmentos__formato_hexadecimal  (
  input  [3:0] in_1
);

  wire a_1_saida_a, b_1_saida_b, c_1_saida_c, d_1_saida_d, e_1_saida_e, f_1_saida_f, g_1_saida_g;

  A a_1 (.in_1(in_1), .SAIDA_A(a_1_saida_a));
  B b_1 (.in_1(in_1), .SAIDA_B(b_1_saida_b));
  C c_1 (.in_1(in_1), .SAIDA_C(c_1_saida_c));
  D d_1 (.in_1(in_1), .SAIDA_D(d_1_saida_d));
  E e_1 (.in_1(in_1), .SAIDA_E(e_1_saida_e));
  F f_1 (.in_1(in_1), .SAIDA_F(f_1_saida_f));
  G g_1 (.in_1(in_1), .SAIDA_G(g_1_saida_g));
  _7_Segment_Display u_7_segment_display_1 (
    .g(g_1_saida_g), .f(f_1_saida_f), .a(a_1_saida_a), .b(b_1_saida_b), .e(e_1_saida_e), .d(d_1_saida_d),
    .c(c_1_saida_c));  // open: dp
endmodule

module \detector_de_sequência_binária  (
  input  ENTRADA,
  output SAIDA
);

  wire and_1_out, clock_1_out, flip_flop_d_1_p3, flip_flop_d_2_p3, not_1_out;

  Clock clock_1 (.out(clock_1_out));
  // Flip_flop_D flip_flop_d_1: pin names not known; wires that end beside it: clock_1_out, ENTRADA, flip_flop_d_1_p3
  not not_1 (not_1_out, ENTRADA);
  and and_1 (and_1_out, flip_flop_d_1_p3, not_1_out);
  // Flip_flop_D flip_flop_d_2: pin names not known; wires that end beside it: clock_1_out, and_1_out, flip_flop_d_2_p3
  and and_2 (SAIDA, flip_flop_d_2_p3, ENTRADA);
endmodule

module extensor_de_4_bits (
  input  [3:0] ENTRADA_DE_4_BITS,
  output [7:0] SAIDA_DE_8_BITS
);


  assign SAIDA_DE_8_BITS = {{5{ENTRADA_DE_4_BITS[3]}}, ENTRADA_DE_4_BITS[2:0]};
endmodule

module Somador_de_8_bits_que_recebe_um_valor_inteiro_e_soma_com_o_valor_4 (
  input  [7:0] ENTRADA_A,
  output [8:0] SAIDA
);

  wire full_adder_1_c_out, full_adder_2_c_out, full_adder_3_c_out, full_adder_4_c_out, full_adder_5_c_out,
       full_adder_6_c_out, full_adder_7_c_out;

  FULL_ADDER full_adder_1 (.C__IN(1'b0), .A(ENTRADA_A[0]), .B(1'b0), .SAIDA(SAIDA[0]), .C_OUT(full_adder_1_c_out));
  FULL_ADDER full_adder_2 (
    .C__IN(full_adder_1_c_out), .A(ENTRADA_A[1]), .B(1'b0), .SAIDA(SAIDA[1]), .C_OUT(full_adder_2_c_out));
  FULL_ADDER full_adder_3 (
    .C__IN(full_adder_2_c_out), .A(ENTRADA_A[2]), .B(1'b1), .SAIDA(SAIDA[2]), .C_OUT(full_adder_3_c_out));
  FULL_ADDER full_adder_4 (
    .C__IN(full_adder_3_c_out), .A(ENTRADA_A[3]), .B(1'b0), .SAIDA(SAIDA[3]), .C_OUT(full_adder_4_c_out));
  FULL_ADDER full_adder_5 (
    .C__IN(full_adder_4_c_out), .A(ENTRADA_A[4]), .B(1'b0), .SAIDA(SAIDA[4]), .C_OUT(full_adder_5_c_out));
  FULL_ADDER full_adder_6 (
    .C__IN(full_adder_5_c_out), .A(ENTRADA_A[5]), .B(1'b0), .SAIDA(SAIDA[5]), .C_OUT(full_adder_6_c_out));
  FULL_ADDER full_adder_7 (
    .C__IN(full_adder_6_c_out), .A(ENTRADA_A[6]), .B(1'b0), .SAIDA(SAIDA[6]), .C_OUT(full_adder_7_c_out));
  FULL_ADDER full_adder_8 (.C__IN(full_adder_7_c_out), .A(ENTRADA_A[7]), .B(1'b0), .SAIDA(SAIDA[7]), .C_OUT(SAIDA[8]));
endmodule

module FULL_ADDER (
  input  C__IN,
  input  A,
  input  B,
  output SAIDA,
  output C_OUT
);

  wire and_1_out, and_2_out, xor_1_out;

  xor xor_1 (xor_1_out, A, B);
  and and_1 (and_1_out, C__IN, xor_1_out);
  and and_2 (and_2_out, A, B);
  xor xor_2 (SAIDA, xor_1_out, C__IN);
  or or_1 (C_OUT, and_1_out, and_2_out);
endmodule

module \Implemente_uma_maquina_de_estados_utilizando_portas_lógicas  (
  input  in_1,
  output out_2
);

  wire and_1_out, and_2_out, clock_1_out, flip_flop_d_1_nq, not_1_out, not_2_out, or_1_out;

  not not_1 (not_1_out, out_2);
  and and_1 (and_1_out, out_2, not_2_out);
  not not_2 (not_2_out, in_1);
  and and_2 (and_2_out, not_1_out, in_1);
  or or_1 (or_1_out, and_2_out, and_1_out);
  Clock clock_1 (.out(clock_1_out));
  Flip_flop_D flip_flop_d_1 (.D(clock_1_out), .Q(out_2), .nQ(flip_flop_d_1_nq));
endmodule

module \Resolva_um_problema_de_otimização_lógica_utilizando_mapas_de_Karnaugh_e_implemente_o_circuito_otimizado  (
  input  A,
  input  B,
  output SAIDA_DO_CIRCUITO_ORIGINAL,
  output SAIDA_DO_CIRCUITO_SIMPLIFICADO
);

  wire and_1_out, and_2_out, not_1_out, not_2_out;

  not not_1 (not_1_out, A);
  not not_2 (not_2_out, B);
  xor xor_1 (SAIDA_DO_CIRCUITO_SIMPLIFICADO, B, A);
  and and_1 (and_1_out, A, not_2_out);
  and and_2 (and_2_out, not_1_out, B);
  or or_1 (SAIDA_DO_CIRCUITO_ORIGINAL, and_1_out, and_2_out);
endmodule

module \Combine_portas_AND__OR_e_NOT_para_criar_a_lógica_de_um_detector_de_paridade_ímpar__entrada_com_número_ímpar_de_1s  (
  input  [3:0] \ENTRADA_DE_NÚMERO_ÍMPA_BiNÁRIO ,
  output SAIDA_DE_0_OU_1
);

  wire and_1_out, and_2_out, and_3_out, and_4_out, and_5_out, and_6_out, and_7_out, and_8_out, not_1_out,
       not_2_out, not_3_out, not_4_out, not_5_out, not_6_out, not_7_out, not_8_out, not_9_out, not_10_out,
       not_11_out, not_12_out, not_13_out, not_14_out, not_15_out, not_16_out;

  not not_1 (not_1_out, \ENTRADA_DE_NÚMERO_ÍMPA_BiNÁRIO [1]);
  not not_2 (not_2_out, \ENTRADA_DE_NÚMERO_ÍMPA_BiNÁRIO [2]);
  not not_3 (not_3_out, \ENTRADA_DE_NÚMERO_ÍMPA_BiNÁRIO [3]);
  not not_4 (not_4_out, \ENTRADA_DE_NÚMERO_ÍMPA_BiNÁRIO [0]);
  not not_5 (not_5_out, \ENTRADA_DE_NÚMERO_ÍMPA_BiNÁRIO [2]);
  not not_6 (not_6_out, \ENTRADA_DE_NÚMERO_ÍMPA_BiNÁRIO [3]);
  not not_7 (not_7_out, \ENTRADA_DE_NÚMERO_ÍMPA_BiNÁRIO [0]);
  not not_8 (not_8_out, \ENTRADA_DE_NÚMERO_ÍMPA_BiNÁRIO [1]);
  not not_9 (not_9_out, \ENTRADA_DE_NÚMERO_ÍMPA_BiNÁRIO [3]);
  not not_10 (not_10_out, \ENTRADA_DE_NÚMERO_ÍMPA_BiNÁRIO [0]);
  not not_11 (not_11_out, \ENTRADA_DE_NÚMERO_ÍMPA_BiNÁRIO [1]);
  not not_12 (not_12_out, \ENTRADA_DE_NÚMERO_ÍMPA_BiNÁRIO [3]);
  not not_13 (not_13_out, \ENTRADA_DE_NÚMERO_ÍMPA_BiNÁRIO [3]);
  not not_14 (not_14_out, \ENTRADA_DE_NÚMERO_ÍMPA_BiNÁRIO [2]);
  not not_15 (not_15_out, \ENTRADA_DE_NÚMERO_ÍMPA_BiNÁRIO [1]);
  not not_16 (not_16_out, \ENTRADA_DE_NÚMERO_ÍMPA_BiNÁRIO [0]);
  and and_1 (and_1_out, \ENTRADA_DE_NÚMERO_ÍMPA_BiNÁRIO [0], not_1_out, not_2_out, not_3_out);
  and and_2 (and_2_out, not_4_out, \ENTRADA_DE_NÚMERO_ÍMPA_BiNÁRIO [1], not_5_out, not_6_out);
  and and_3 (and_3_out, not_7_out, not_8_out, \ENTRADA_DE_NÚMERO_ÍMPA_BiNÁRIO [2], not_9_out);
  and and_4 (and_4_out, not_10_out, not_11_out, not_12_out, \ENTRADA_DE_NÚMERO_ÍMPA_BiNÁRIO [3]);
  and and_5 (and_5_out, \ENTRADA_DE_NÚMERO_ÍMPA_BiNÁRIO [0], \ENTRADA_DE_NÚMERO_ÍMPA_BiNÁRIO [1], \ENTRADA_DE_NÚMERO_ÍMPA_BiNÁRIO [2], not_13_out);
  and and_6 (and_6_out, \ENTRADA_DE_NÚMERO_ÍMPA_BiNÁRIO [0], \ENTRADA_DE_NÚMERO_ÍMPA_BiNÁRIO [1], not_14_out, \ENTRADA_DE_NÚMERO_ÍMPA_BiNÁRIO [3]);
  and and_7 (and_7_out, \ENTRADA_DE_NÚMERO_ÍMPA_BiNÁRIO [0], not_15_out, \ENTRADA_DE_NÚMERO_ÍMPA_BiNÁRIO [2], \ENTRADA_DE_NÚMERO_ÍMPA_BiNÁRIO [3]);
  and and_8 (and_8_out, not_16_out, \ENTRADA_DE_NÚMERO_ÍMPA_BiNÁRIO [1], \ENTRADA_DE_NÚMERO_ÍMPA_BiNÁRIO [2], \ENTRADA_DE_NÚMERO_ÍMPA_BiNÁRIO [3]);
  or or_1 (SAIDA_DE_0_OU_1, and_1_out, and_2_out, and_3_out, and_4_out, and_5_out, and_6_out, and_7_out, and_8_out);
endmodule

module A (
  input  [3:0] in_1,
  output SAIDA_A
);

  wire and_1_out, and_2_out, and_3_out, and_4_out, and_5_out, and_6_out, not_1_out, not_2_out, not_3_out,
       not_4_out, not_5_out, not_6_out, not_7_out;

  not not_1 (not_1_out, in_1[2]);
  not not_2 (not_2_out, in_1[0]);
  not not_3 (not_3_out, in_1[3]);
  not not_4 (not_4_out, in_1[3]);
  not not_5 (not_5_out, in_1[0]);
  not not_6 (not_6_out, in_1[2]);
  not not_7 (not_7_out, in_1[1]);
  and and_1 (and_1_out, not_1_out, not_2_out);
  and and_2 (and_2_out, not_3_out, in_1[1]);
  and and_3 (and_3_out, not_4_out, in_1[2], in_1[0]);
  and and_4 (and_4_out, in_1[2], in_1[1]);
  and and_5 (and_5_out, in_1[3], not_5_out);
  and and_6 (and_6_out, in_1[3], not_6_out, not_7_out);
  or or_1 (SAIDA_A, and_1_out, and_2_out, and_3_out, and_4_out, and_5_out, and_6_out);
endmodule

module B (
  input  [3:0] in_1,
  output SAIDA_B
);

  wire and_1_out, and_2_out, and_3_out, and_4_out, and_5_out, not_1_out, not_2_out, not_3_out, not_4_out,
       not_5_out, not_6_out, not_7_out, not_8_out, not_9_out;

  not not_1 (not_1_out, in_1[1]);
  not not_2 (not_2_out, in_1[2]);
  not not_3 (not_3_out, in_1[0]);
  not not_4 (not_4_out, in_1[3]);
  not not_5 (not_5_out, in_1[1]);
  not not_6 (not_6_out, in_1[0]);
  not not_7 (not_7_out, in_1[3]);
  not not_8 (not_8_out, in_1[3]);
  not not_9 (not_9_out, in_1[2]);
  and and_1 (and_1_out, in_1[3], not_1_out, in_1[0]);
  and and_2 (and_2_out, not_2_out, not_3_out);
  and and_3 (and_3_out, not_4_out, not_5_out, not_6_out);
  and and_4 (and_4_out, not_7_out, in_1[1], in_1[0]);
  and and_5 (and_5_out, not_8_out, not_9_out);
  or or_1 (SAIDA_B, and_1_out, and_2_out, and_3_out, and_4_out, and_5_out);
endmodule

module C (
  input  [3:0] in_1,
  output SAIDA_C
);

  wire and_1_out, and_2_out, and_3_out, and_4_out, and_5_out, not_1_out, not_2_out, not_3_out, not_4_out,
       not_5_out, not_6_out;

  not not_1 (not_1_out, in_1[1]);
  not not_2 (not_2_out, in_1[3]);
  not not_3 (not_3_out, in_1[2]);
  not not_4 (not_4_out, in_1[3]);
  not not_5 (not_5_out, in_1[1]);
  not not_6 (not_6_out, in_1[3]);
  and and_1 (and_1_out, not_1_out, in_1[0]);
  and and_2 (and_2_out, not_2_out, in_1[2]);
  and and_3 (and_3_out, in_1[3], not_3_out);
  and and_4 (and_4_out, not_4_out, not_5_out);
  and and_5 (and_5_out, not_6_out, in_1[0]);
  or or_1 (SAIDA_C, and_1_out, and_2_out, and_3_out, and_4_out, and_5_out);
endmodule

module D (
  input  [3:0] in_1,
  output SAIDA_D
);

  wire and_1_out, and_2_out, and_3_out, and_4_out, and_5_out, not_1_out, not_2_out, not_3_out, not_4_out,
       not_5_out, not_6_out, not_7_out;

  not not_1 (not_1_out, in_1[1]);
  not not_2 (not_2_out, in_1[2]);
  not not_3 (not_3_out, in_1[0]);
  not not_4 (not_4_out, in_1[1]);
  not not_5 (not_5_out, in_1[3]);
  not not_6 (not_6_out, in_1[2]);
  not not_7 (not_7_out, in_1[0]);
  and and_1 (and_1_out, in_1[2], not_1_out, in_1[0]);
  and and_2 (and_2_out, not_2_out, in_1[1], in_1[0]);
  and and_3 (and_3_out, in_1[2], in_1[1], not_3_out);
  and and_4 (and_4_out, in_1[3], not_4_out);
  and and_5 (and_5_out, not_5_out, not_6_out, not_7_out);
  or or_1 (SAIDA_D, and_1_out, and_2_out, and_3_out, and_4_out, and_5_out);
endmodule

module E (
  input  [3:0] in_1,
  output SAIDA_E
);

  wire and_1_out, and_2_out, and_3_out, and_4_out, not_1_out, not_2_out, not_3_out;

  not not_1 (not_1_out, in_1[2]);
  not not_2 (not_2_out, in_1[0]);
  not not_3 (not_3_out, in_1[0]);
  and and_1 (and_1_out, not_1_out, not_2_out);
  and and_2 (and_2_out, not_3_out, in_1[1]);
  and and_3 (and_3_out, in_1[3], in_1[1]);
  and and_4 (and_4_out, in_1[3], in_1[2]);
  or or_1 (SAIDA_E, and_1_out, and_2_out, and_3_out, and_4_out);
endmodule

module F (
  input  [3:0] in_1,
  output SAIDA_F
);

  wire and_1_out, and_2_out, and_3_out, and_4_out, and_5_out, not_1_out, not_2_out, not_3_out, not_4_out,
       not_5_out, not_6_out;

  not not_1 (not_1_out, in_1[1]);
  not not_2 (not_2_out, in_1[0]);
  not not_3 (not_3_out, in_1[0]);
  not not_4 (not_4_out, in_1[3]);
  not not_5 (not_5_out, in_1[1]);
  not not_6 (not_6_out, in_1[2]);
  and and_1 (and_1_out, not_1_out, not_2_out);
  and and_2 (and_2_out, not_3_out, in_1[2]);
  and and_3 (and_3_out, not_4_out, in_1[2], not_5_out);
  and and_4 (and_4_out, in_1[3], not_6_out);
  and and_5 (and_5_out, in_1[3], in_1[1]);
  or or_1 (SAIDA_F, and_1_out, and_2_out, and_3_out, and_4_out, and_5_out);
endmodule

module G (
  input  [3:0] in_1,
  output SAIDA_G
);

  wire and_1_out, and_2_out, and_3_out, and_4_out, and_5_out, not_1_out, not_2_out, not_3_out, not_4_out,
       not_5_out;

  not not_1 (not_1_out, in_1[2]);
  not not_2 (not_2_out, in_1[2]);
  not not_3 (not_3_out, in_1[0]);
  not not_4 (not_4_out, in_1[3]);
  not not_5 (not_5_out, in_1[1]);
  and and_1 (and_1_out, not_1_out, in_1[1]);
  and and_2 (and_2_out, not_2_out, in_1[3]);
  and and_3 (and_3_out, in_1[3], in_1[0]);
  and and_4 (and_4_out, in_1[1], not_3_out);
  and and_5 (and_5_out, not_4_out, in_1[2], not_5_out);
  or or_1 (SAIDA_G, and_1_out, and_2_out, and_3_out, and_4_out, and_5_out);
endmodule
